// Logisim project 8_bit_ALU.circ as structural Verilog: 22 circuits, main circuit main
module main (
);

  CPU_ALU cpu_alu_1 ();  // open: PASS_A, Input_A, Input_B, a, b, c, Sub, A_INC_ONE, A_DEC_ONE, carry_in, carry_out, zero, Negitive, out_16, equal, b_larger, a_larger
endmodule

module CPU_ALU (
  input  [7:0] Input_A,
  input  [7:0] Input_B,
  input  carry_in,
  input  Sub,
  input  A_INC_ONE,
  input  A_DEC_ONE,
  input  PASS_A,
  input  a,
  input  b,
  input  c,
  output a_larger,
  output equal,
  output b_larger,
  output zero,
  output Negitive,
  output [7:0] out_16,
  output carry_out
);

  wire and_1_out, and_2_out, cpu_adder_8_1_carry_out_e418b9d9, cpu_shl_1_shift_out_6b808c51,
       cpu_shr_1_shift_out_6b808c51, cpu_sub_1_cout;
  wire [7:0] adder_1_out, cpu_adder_8_1_out_5, cpu_and_1_o, cpu_decoder_3x8_1_o, cpu_e_1_out_3,
       cpu_not_1_out_2, cpu_or_1_l_0_b268df69, cpu_shl_1_o, cpu_shr_1_o, cpu_sub_1_result, multiplexer_1_out,
       multiplexer_2_out, multiplexer_3_out, subtractor_1_out, xor_le_8_1_out_3;

  XOR_LE_8 xor_le_8_1 (.a(Input_A), .b(Input_B), .larger(a_larger), .equal(equal), .out_3(xor_le_8_1_out_3));
  CPU_AND cpu_and_1 (.b(Input_B), .a(Input_A), .o(cpu_and_1_o));
  CPU_NOT cpu_not_1 (.i(Input_A), .out_2(cpu_not_1_out_2));
  CPU_SHL cpu_shl_1 (
    .shift_in_a7f48d08(carry_in), .i(Input_A), .shift_out_6b808c51(cpu_shl_1_shift_out_6b808c51),
    .o(cpu_shl_1_o));
  CPU_SHR cpu_shr_1 (
    .shift_in_a7f48d08(carry_in), .i(Input_A), .shift_out_6b808c51(cpu_shr_1_shift_out_6b808c51),
    .o(cpu_shr_1_o));
  CPU_ADDER_8 cpu_adder_8_1 (
    .b(Input_B), .a(Input_A), .carry_in_270e3c82(carry_in),
    .carry_out_e418b9d9(cpu_adder_8_1_carry_out_e418b9d9), .out_5(cpu_adder_8_1_out_5));
  Adder adder_1 (.a(Input_A), .b(8'h1), .out(adder_1_out), .cin(carry_in));  // open: cout
  Subtractor subtractor_1 (.a(Input_A), .b(8'h1), .out(subtractor_1_out));  // open: bin, bout
  CPU_OR cpu_or_1 (.a(Input_A), .b(Input_B), .L_0_b268df69(cpu_or_1_l_0_b268df69));
  CPU_SUB cpu_sub_1 (.A(Input_A), .B(Input_B), .Cin(carry_in), .Cout(cpu_sub_1_cout), .Result(cpu_sub_1_result));
  Multiplexer #(.enable("true"), .width(8)) multiplexer_1 (
    .in0(cpu_adder_8_1_out_5), .in1(cpu_sub_1_result), .out(multiplexer_1_out), .sel(Sub));  // open: en
  CPU_E cpu_e_1 (.in_1(xor_le_8_1_out_3), .in_2(cpu_decoder_3x8_1_o[6]), .out_3(cpu_e_1_out_3));
  CPU_E cpu_e_2 (.in_1(cpu_or_1_l_0_b268df69), .in_2(cpu_decoder_3x8_1_o[5]), .out_3(cpu_e_1_out_3));
  CPU_E cpu_e_3 (.in_1(cpu_and_1_o), .in_2(cpu_decoder_3x8_1_o[4]), .out_3(cpu_e_1_out_3));
  CPU_E cpu_e_4 (.in_1(cpu_not_1_out_2), .in_2(cpu_decoder_3x8_1_o[3]), .out_3(cpu_e_1_out_3));
  CPU_E cpu_e_5 (.in_1(cpu_shl_1_o), .in_2(cpu_decoder_3x8_1_o[2]), .out_3(cpu_e_1_out_3));
  CPU_E cpu_e_6 (.in_1(cpu_shr_1_o), .in_2(cpu_decoder_3x8_1_o[1]), .out_3(cpu_e_1_out_3));
  Multiplexer #(.enable("true"), .width(8)) multiplexer_2 (
    .in0(multiplexer_1_out), .in1(adder_1_out), .out(multiplexer_2_out), .sel(A_INC_ONE));  // open: en
  CPU_DECODER_3x8 cpu_decoder_3x8_1 (.c(c), .b(b), .a(a), .o(cpu_decoder_3x8_1_o));
  Multiplexer #(.enable("true"), .width(8)) multiplexer_3 (
    .in0(multiplexer_2_out), .in1(subtractor_1_out), .out(multiplexer_3_out), .sel(A_DEC_ONE));  // open: en
  CPU_E cpu_e_7 (.in_1(multiplexer_3_out), .in_2(cpu_decoder_3x8_1_o[0]), .out_3(cpu_e_1_out_3));
  and and_1 (and_1_out, cpu_shl_1_shift_out_6b808c51, cpu_decoder_3x8_1_o[2]);
  assign carry_out = cpu_decoder_3x8_1_o[2] ? and_1_out : 1'bz;  // Controlled_Buffer controlled_buffer_1
  and and_2 (and_2_out, cpu_shr_1_shift_out_6b808c51, cpu_decoder_3x8_1_o[1]);
  assign carry_out = cpu_decoder_3x8_1_o[1] ? and_2_out : 1'bz;  // Controlled_Buffer controlled_buffer_2
  Multiplexer #(.enable("true")) multiplexer_4 (
    .in0(cpu_adder_8_1_carry_out_e418b9d9), .in1(cpu_sub_1_cout), .out(carry_out), .sel(Sub));  // open: en
  Multiplexer #(.enable("true"), .width(8)) multiplexer_5 (
    .in0(cpu_e_1_out_3), .in1(Input_A), .out(out_16), .sel(PASS_A));  // open: en
  CPU_LESS cpu_less_1 (.A_large(a_larger), .equal(equal), .A_less(b_larger));
  CPU_Z cpu_z_1 (.i(cpu_e_1_out_3), .o(zero));
  CUP_N cup_n_1 (.i(cpu_e_1_out_3), .out_2(Negitive));

  // Notes on the sheet:
  //   carry_out: pull=down
  //   zero: pull=down
  //   out_16: pull=down
  //   equal: pull=down
  //   a_larger: pull=down
  //   Input_A: pull=down
  //   Input_B: pull=down
  //   a: pull=down
  //   b: pull=down
  //   c: pull=down
  //   carry_in: pull=down
endmodule

module CPU_XOR_1 (
  input  a,
  input  b,
  output o
);

  wire nand_1_out, nand_2_out, not_1_out, not_2_out;

  not not_1 (not_1_out, a);
  not not_2 (not_2_out, b);
  nand nand_1 (nand_1_out, not_1_out, b);
  nand nand_2 (nand_2_out, a, not_2_out);
  nand nand_3 (o, nand_1_out, nand_2_out);
endmodule

module CPU_XOR_LE_1 (
  input  a_larger_94e4cd8d,
  input  above_equal_21927267,
  input  a,
  input  b,
  output c,
  output equal,
  output a_large
);

  wire and_2_out, not_1_out;

  CPU_XOR_1 cpu_xor_1_1 (.a(a), .b(b), .o(c));
  not not_1 (not_1_out, c);
  and and_1 (equal, not_1_out, above_equal_21927267);
  and and_2 (and_2_out, above_equal_21927267, a, c);
  or or_1 (a_large, and_2_out, a_larger_94e4cd8d);
endmodule

module XOR_LE_8 (
  input  [7:0] a,
  input  [7:0] b,
  output [7:0] out_3,
  output larger,
  output equal
);

  wire cpu_xor_le_1_1_a_large, cpu_xor_le_1_1_equal, cpu_xor_le_1_2_a_large, cpu_xor_le_1_2_equal,
       cpu_xor_le_1_3_a_large, cpu_xor_le_1_3_equal, cpu_xor_le_1_4_a_large, cpu_xor_le_1_4_equal,
       cpu_xor_le_1_5_a_large, cpu_xor_le_1_5_equal, cpu_xor_le_1_6_a_large, cpu_xor_le_1_6_equal,
       cpu_xor_le_1_7_a_large, cpu_xor_le_1_7_equal;

  CPU_XOR_LE_1 cpu_xor_le_1_1 (
    .a(a[7]), .b(b[7]), .above_equal_21927267(1'b1), .a_larger_94e4cd8d(1'b0), .equal(cpu_xor_le_1_1_equal),
    .a_large(cpu_xor_le_1_1_a_large), .c(out_3[7]));
  CPU_XOR_LE_1 cpu_xor_le_1_2 (
    .a(a[6]), .b(b[6]), .above_equal_21927267(cpu_xor_le_1_1_equal),
    .a_larger_94e4cd8d(cpu_xor_le_1_1_a_large), .equal(cpu_xor_le_1_2_equal),
    .a_large(cpu_xor_le_1_2_a_large), .c(out_3[6]));
  CPU_XOR_LE_1 cpu_xor_le_1_3 (
    .a(a[5]), .b(b[5]), .above_equal_21927267(cpu_xor_le_1_2_equal),
    .a_larger_94e4cd8d(cpu_xor_le_1_2_a_large), .equal(cpu_xor_le_1_3_equal),
    .a_large(cpu_xor_le_1_3_a_large), .c(out_3[5]));
  CPU_XOR_LE_1 cpu_xor_le_1_4 (
    .a(a[4]), .b(b[4]), .above_equal_21927267(cpu_xor_le_1_3_equal),
    .a_larger_94e4cd8d(cpu_xor_le_1_3_a_large), .equal(cpu_xor_le_1_4_equal),
    .a_large(cpu_xor_le_1_4_a_large), .c(out_3[4]));
  CPU_XOR_LE_1 cpu_xor_le_1_5 (
    .a(a[3]), .b(b[3]), .above_equal_21927267(cpu_xor_le_1_4_equal),
    .a_larger_94e4cd8d(cpu_xor_le_1_4_a_large), .equal(cpu_xor_le_1_5_equal),
    .a_large(cpu_xor_le_1_5_a_large), .c(out_3[3]));
  CPU_XOR_LE_1 cpu_xor_le_1_6 (
    .a(a[2]), .b(b[2]), .above_equal_21927267(cpu_xor_le_1_5_equal),
    .a_larger_94e4cd8d(cpu_xor_le_1_5_a_large), .equal(cpu_xor_le_1_6_equal),
    .a_large(cpu_xor_le_1_6_a_large), .c(out_3[2]));
  CPU_XOR_LE_1 cpu_xor_le_1_7 (
    .a(a[1]), .b(b[1]), .above_equal_21927267(cpu_xor_le_1_6_equal),
    .a_larger_94e4cd8d(cpu_xor_le_1_6_a_large), .equal(cpu_xor_le_1_7_equal),
    .a_large(cpu_xor_le_1_7_a_large), .c(out_3[1]));
  CPU_XOR_LE_1 cpu_xor_le_1_8 (
    .a(a[0]), .b(b[0]), .above_equal_21927267(cpu_xor_le_1_7_equal),
    .a_larger_94e4cd8d(cpu_xor_le_1_7_a_large), .equal(equal), .a_large(larger), .c(out_3[0]));
endmodule

module CPU_OR (
  input  [7:0] a,
  input  [7:0] b,
  output [7:0] L_0_b268df69
);

  or or_1 (L_0_b268df69[0], a[0], b[0]);
  or or_2 (L_0_b268df69[1], a[1], b[1]);
  or or_3 (L_0_b268df69[2], a[2], b[2]);
  or or_4 (L_0_b268df69[3], a[3], b[3]);
  or or_5 (L_0_b268df69[4], a[4], b[4]);
  or or_6 (L_0_b268df69[5], a[5], b[5]);
  or or_7 (L_0_b268df69[6], a[6], b[6]);
  or or_8 (L_0_b268df69[7], a[7], b[7]);
endmodule

module CPU_AND (
  input  [7:0] a,
  input  [7:0] b,
  output [7:0] o
);

  and and_1 (o[0], a[0], b[0]);
  and and_2 (o[1], a[1], b[1]);
  and and_3 (o[2], a[2], b[2]);
  and and_4 (o[3], a[3], b[3]);
  and and_5 (o[4], a[4], b[4]);
  and and_6 (o[5], a[5], b[5]);
  and and_7 (o[6], a[6], b[6]);
  and and_8 (o[7], a[7], b[7]);
endmodule

module CPU_NOT (
  input  [7:0] i,
  output [7:0] out_2
);

  not not_1 (out_2[0], i[0]);
  not not_2 (out_2[1], i[1]);
  not not_3 (out_2[2], i[2]);
  not not_4 (out_2[3], i[3]);
  not not_5 (out_2[4], i[4]);
  not not_6 (out_2[5], i[5]);
  not not_7 (out_2[6], i[6]);
  not not_8 (out_2[7], i[7]);
endmodule

module CPU_SHL (
  input  shift_in_a7f48d08,
  input  [7:0] i,
  output [7:0] o,
  output shift_out_6b808c51
);

  wire [6:0] cpu_register_8_1_l_0_b268df69;

  CPU_REGISTER_8 cpu_register_8_1 (
    .i(i), .s(1'b1), .e(1'b1), .L_0_b268df69({shift_out_6b808c51, cpu_register_8_1_l_0_b268df69}));  // open: REG
  CPU_REGISTER_8 cpu_register_8_2 (
    .i({cpu_register_8_1_l_0_b268df69, shift_in_a7f48d08}), .s(1'b1), .e(1'b1), .L_0_b268df69(o));  // open: REG
endmodule

module CPU_SHR (
  input  [7:0] i,
  input  shift_in_a7f48d08,
  output shift_out_6b808c51,
  output [7:0] o
);

  wire [7:1] cpu_register_8_1_l_0_b268df69;

  CPU_REGISTER_8 cpu_register_8_1 (
    .i(i), .s(1'b1), .e(1'b1), .L_0_b268df69({cpu_register_8_1_l_0_b268df69, shift_out_6b808c51}));  // open: REG
  CPU_REGISTER_8 cpu_register_8_2 (
    .i({shift_in_a7f48d08, cpu_register_8_1_l_0_b268df69}), .s(1'b1), .e(1'b1), .L_0_b268df69(o));  // open: REG
endmodule

module CPU_ADDER (
  input  a,
  input  b,
  input  carry_in_270e3c82,
  output sum,
  output carry_out_e418b9d9
);

  wire and_1_out, and_2_out, cpu_xor_1_1_o;

  CPU_XOR_1 cpu_xor_1_1 (.a(a), .b(b), .o(cpu_xor_1_1_o));
  and and_1 (and_1_out, carry_in_270e3c82, cpu_xor_1_1_o);
  and and_2 (and_2_out, a, b);
  CPU_XOR_1 cpu_xor_1_2 (.a(cpu_xor_1_1_o), .b(carry_in_270e3c82), .o(sum));
  or or_1 (carry_out_e418b9d9, and_1_out, and_2_out);
endmodule

module CPU_ADDER_8 (
  input  [7:0] a,
  input  [7:0] b,
  input  carry_in_270e3c82,
  output carry_out_e418b9d9,
  output [7:0] out_5
);

  wire cpu_adder_2_carry_out_e418b9d9, cpu_adder_3_carry_out_e418b9d9, cpu_adder_4_carry_out_e418b9d9,
       cpu_adder_5_carry_out_e418b9d9, cpu_adder_6_carry_out_e418b9d9, cpu_adder_7_carry_out_e418b9d9,
       cpu_adder_8_carry_out_e418b9d9;

  CPU_ADDER cpu_adder_1 (
    .carry_in_270e3c82(cpu_adder_2_carry_out_e418b9d9), .a(a[7]), .b(b[7]), .sum(out_5[7]),
    .carry_out_e418b9d9(carry_out_e418b9d9));
  CPU_ADDER cpu_adder_2 (
    .carry_in_270e3c82(cpu_adder_3_carry_out_e418b9d9), .a(a[6]), .b(b[6]), .sum(out_5[6]),
    .carry_out_e418b9d9(cpu_adder_2_carry_out_e418b9d9));
  CPU_ADDER cpu_adder_3 (
    .carry_in_270e3c82(cpu_adder_4_carry_out_e418b9d9), .a(a[5]), .b(b[5]), .sum(out_5[5]),
    .carry_out_e418b9d9(cpu_adder_3_carry_out_e418b9d9));
  CPU_ADDER cpu_adder_4 (
    .carry_in_270e3c82(cpu_adder_5_carry_out_e418b9d9), .a(a[4]), .b(b[4]), .sum(out_5[4]),
    .carry_out_e418b9d9(cpu_adder_4_carry_out_e418b9d9));
  CPU_ADDER cpu_adder_5 (
    .carry_in_270e3c82(cpu_adder_6_carry_out_e418b9d9), .a(a[3]), .b(b[3]), .sum(out_5[3]),
    .carry_out_e418b9d9(cpu_adder_5_carry_out_e418b9d9));
  CPU_ADDER cpu_adder_6 (
    .carry_in_270e3c82(cpu_adder_7_carry_out_e418b9d9), .a(a[2]), .b(b[2]), .sum(out_5[2]),
    .carry_out_e418b9d9(cpu_adder_6_carry_out_e418b9d9));
  CPU_ADDER cpu_adder_7 (
    .carry_in_270e3c82(cpu_adder_8_carry_out_e418b9d9), .a(a[1]), .b(b[1]), .sum(out_5[1]),
    .carry_out_e418b9d9(cpu_adder_7_carry_out_e418b9d9));
  CPU_ADDER cpu_adder_8 (
    .carry_in_270e3c82(carry_in_270e3c82), .a(a[0]), .b(b[0]), .sum(out_5[0]),
    .carry_out_e418b9d9(cpu_adder_8_carry_out_e418b9d9));
endmodule

module CPU_SUB (
  input  Cin,
  input  [7:0] A,
  input  [7:0] B,
  output [7:0] Result,
  output Cout
);

  wire subtractor_1_bout, subtractor_2_bout, subtractor_3_bout, subtractor_4_bout, subtractor_5_bout,
       subtractor_6_bout, subtractor_7_bout;

  Subtractor #(.width(1)) subtractor_1 (.a(A[0]), .b(B[0]), .out(Result[0]), .bin(Cin), .bout(subtractor_1_bout));
  Subtractor #(.width(1)) subtractor_2 (
    .a(A[1]), .b(B[1]), .out(Result[1]), .bin(subtractor_1_bout), .bout(subtractor_2_bout));
  Subtractor #(.width(1)) subtractor_3 (
    .a(A[2]), .b(B[2]), .out(Result[2]), .bin(subtractor_2_bout), .bout(subtractor_3_bout));
  Subtractor #(.width(1)) subtractor_4 (
    .a(A[3]), .b(B[3]), .out(Result[3]), .bin(subtractor_3_bout), .bout(subtractor_4_bout));
  Subtractor #(.width(1)) subtractor_5 (
    .a(A[4]), .b(B[4]), .out(Result[4]), .bin(subtractor_4_bout), .bout(subtractor_5_bout));
  Subtractor #(.width(1)) subtractor_6 (
    .a(A[5]), .b(B[5]), .out(Result[5]), .bin(subtractor_5_bout), .bout(subtractor_6_bout));
  Subtractor #(.width(1)) subtractor_7 (
    .a(A[6]), .b(B[6]), .out(Result[6]), .bin(subtractor_6_bout), .bout(subtractor_7_bout));
  Subtractor #(.width(1)) subtractor_8 (.a(A[7]), .b(B[7]), .out(Result[7]), .bin(subtractor_7_bout), .bout(Cout));
endmodule

module CPU_REGISTER_8 (
  input  [7:0] i,
  input  s,
  input  e,
  output [7:0] REG,
  output [7:0] L_0_b268df69
);

  wire [7:0] cpu_enable_8_1_out_3;

  CPU_MEM_8 cpu_mem_8_1 (.s(s), .out_3(REG));  // open: in_1
  CPU_ENABLE_8 cpu_enable_8_1 (.in_1(REG), .in_2(e), .out_3(cpu_enable_8_1_out_3));
  assign L_0_b268df69 = e ? cpu_enable_8_1_out_3 : 8'bz;  // Controlled_Buffer controlled_buffer_1

  // Notes on the sheet:
  //   i: pull=down
  //   s: pull=down
  //   e: pull=down
  //   L_0_b268df69: pull=down
endmodule

module CPU_Z (
  input  [7:0] i,
  output o
);

  wire or_1_out;

  or or_1 (or_1_out, i[0], i[1], i[2], i[3], i[4], i[5], i[6], i[7]);
  not not_1 (o, or_1_out);
endmodule

module CUP_N (
  input  [7:0] i,
  output out_2
);


  assign out_2 = i[7];
endmodule

module CPU_E (
  input  [7:0] in_1,
  input  in_2,
  output [7:0] out_3
);

  wire and_1_out, and_2_out, and_3_out, and_4_out, and_5_out, and_6_out, and_7_out, and_8_out;

  and and_1 (and_1_out, in_1[0], in_2);
  assign out_3[0] = in_2 ? and_1_out : 1'bz;  // Controlled_Buffer controlled_buffer_1
  and and_2 (and_2_out, in_1[1], in_2);
  assign out_3[1] = in_2 ? and_2_out : 1'bz;  // Controlled_Buffer controlled_buffer_2
  and and_3 (and_3_out, in_1[2], in_2);
  assign out_3[2] = in_2 ? and_3_out : 1'bz;  // Controlled_Buffer controlled_buffer_3
  and and_4 (and_4_out, in_1[3], in_2);
  assign out_3[3] = in_2 ? and_4_out : 1'bz;  // Controlled_Buffer controlled_buffer_4
  and and_5 (and_5_out, in_1[4], in_2);
  assign out_3[4] = in_2 ? and_5_out : 1'bz;  // Controlled_Buffer controlled_buffer_5
  and and_6 (and_6_out, in_1[5], in_2);
  assign out_3[5] = in_2 ? and_6_out : 1'bz;  // Controlled_Buffer controlled_buffer_6
  and and_7 (and_7_out, in_1[6], in_2);
  assign out_3[6] = in_2 ? and_7_out : 1'bz;  // Controlled_Buffer controlled_buffer_7
  and and_8 (and_8_out, in_1[7], in_2);
  assign out_3[7] = in_2 ? and_8_out : 1'bz;  // Controlled_Buffer controlled_buffer_8
endmodule

module CPU_MEM_1 (
  input  in_1,
  input  in_2,
  output out_3
);

  wire nand_1_out, nand_2_out, nand_4_out;

  nand nand_1 (nand_1_out, in_1, in_2);
  nand nand_2 (nand_2_out, nand_1_out, in_2);
  nand nand_3 (out_3, nand_1_out, nand_4_out);
  nand nand_4 (nand_4_out, out_3, nand_2_out);

  // Notes on the sheet:
  //   in_2: pull=down
  //   in_1: pull=down
endmodule

module CPU_MEM_8 (
  input  [7:0] in_1,
  input  s,
  output [7:0] out_3
);

  CPU_MEM_1 cpu_mem_1_1 (.in_2(s), .in_1(in_1[0]), .out_3(out_3[0]));
  CPU_MEM_1 cpu_mem_1_2 (.in_2(s), .in_1(in_1[1]), .out_3(out_3[1]));
  CPU_MEM_1 cpu_mem_1_3 (.in_2(s), .in_1(in_1[2]), .out_3(out_3[2]));
  CPU_MEM_1 cpu_mem_1_4 (.in_2(s), .in_1(in_1[3]), .out_3(out_3[3]));
  CPU_MEM_1 cpu_mem_1_5 (.in_2(s), .in_1(in_1[4]), .out_3(out_3[4]));
  CPU_MEM_1 cpu_mem_1_6 (.in_2(s), .in_1(in_1[5]), .out_3(out_3[5]));
  CPU_MEM_1 cpu_mem_1_7 (.in_2(s), .in_1(in_1[6]), .out_3(out_3[6]));
  CPU_MEM_1 cpu_mem_1_8 (.in_2(s), .in_1(in_1[7]), .out_3(out_3[7]));

  // Notes on the sheet:
  //   in_1: pull=down
  //   s: pull=down
  //   out_3: pull=down
endmodule

module CPU_ENABLE_8 (
  input  [7:0] in_1,
  input  in_2,
  output [7:0] out_3
);

  wire and_1_out, and_2_out, and_3_out, and_4_out, and_5_out, and_6_out, and_7_out, and_8_out;

  and and_1 (and_1_out, in_1[0], in_2);
  assign out_3[0] = in_2 ? and_1_out : 1'bz;  // Controlled_Buffer controlled_buffer_1
  and and_2 (and_2_out, in_1[1], in_2);
  assign out_3[1] = in_2 ? and_2_out : 1'bz;  // Controlled_Buffer controlled_buffer_2
  and and_3 (and_3_out, in_1[2], in_2);
  assign out_3[2] = in_2 ? and_3_out : 1'bz;  // Controlled_Buffer controlled_buffer_3
  and and_4 (and_4_out, in_1[3], in_2);
  assign out_3[3] = in_2 ? and_4_out : 1'bz;  // Controlled_Buffer controlled_buffer_4
  and and_5 (and_5_out, in_1[4], in_2);
  assign out_3[4] = in_2 ? and_5_out : 1'bz;  // Controlled_Buffer controlled_buffer_5
  and and_6 (and_6_out, in_1[5], in_2);
  assign out_3[5] = in_2 ? and_6_out : 1'bz;  // Controlled_Buffer controlled_buffer_6
  and and_7 (and_7_out, in_1[6], in_2);
  assign out_3[6] = in_2 ? and_7_out : 1'bz;  // Controlled_Buffer controlled_buffer_7
  and and_8 (and_8_out, in_1[7], in_2);
  assign out_3[7] = in_2 ? and_8_out : 1'bz;  // Controlled_Buffer controlled_buffer_8
endmodule

module CPU_DECODER_3x8 (
  input  c,
  input  b,
  input  a,
  output [7:0] o
);

  wire not_1_out, not_2_out, not_3_out;

  not not_1 (not_1_out, a);
  not not_2 (not_2_out, b);
  not not_3 (not_3_out, c);
  and and_1 (o[0], not_3_out, not_2_out, not_1_out);
  and and_2 (o[1], not_3_out, not_2_out, a);
  and and_3 (o[2], not_3_out, b, not_1_out);
  and and_4 (o[3], not_3_out, b, a);
  and and_5 (o[4], c, not_2_out, not_1_out);
  and and_6 (o[5], c, not_2_out, a);
  and and_7 (o[6], c, b, not_1_out);
  and and_8 (o[7], c, b, a);

  // Notes on the sheet:
  //   c: pull=down
  //   b: pull=down
  //   a: pull=down
  //   o: pull=down
  //   msb
  //   lsb
endmodule

module CPU_LESS (
  input  A_large,
  input  equal,
  output A_less
);

  wire or_1_out;

  or or_1 (or_1_out, A_large, equal);
  not not_1 (A_less, or_1_out);
endmodule
